// Logisim project Guess The Number XTREME.circ as structural Verilog
module Cronometro (
  input  CLK,
  input  PAUSE,
  input  CLEAR,
  output [3:0] DM,
  output [3:0] UM,
  output [3:0] DS_prime,
  output [3:0] US,
  output END
);

  wire and_1_out, decsm_2_vai1, unitsm_1_vai1, unitsm_2_vai1;
  wire [3:0] adder_1_out, decsm_1_s0, decsm_2_s0, register_1_q, register_2_q, register_3_q, register_4_q,
       subtractor_1_out, subtractor_2_out, subtractor_3_out, unitsm_1_s0, unitsm_2_s0;

  and and_1 (and_1_out, CLK, ~PAUSE);  // AND_Gate
  Hex_Digit_Display hex_digit_display_1 (.value(decsm_1_s0));  // open: dp
  decSM decsm_1 (
    .A3(subtractor_1_out[3]), .A2(subtractor_1_out[2]), .A1(subtractor_1_out[1]), .A0(subtractor_1_out[0]),
    .S3(decsm_1_s0[3]), .S2(decsm_1_s0[2]), .S1(decsm_1_s0[1]), .S0(decsm_1_s0[0]));  // open: VAI1
  Register #(.width(4)) register_1 (.D(decsm_1_s0), .Q(register_1_q), .clk(and_1_out), .clr(CLEAR));  // open: en
  Subtractor #(.width(4)) subtractor_1 (
    .a(register_1_q), .b(4'b0000), .out(subtractor_1_out), .bin(unitsm_1_vai1));  // open: bout
  Hex_Digit_Display hex_digit_display_2 (.value(unitsm_1_s0));  // open: dp
  Register #(.width(4)) register_2 (.D(unitsm_1_s0), .Q(register_2_q), .clk(and_1_out), .clr(CLEAR));  // open: en
  unitSM unitsm_1 (
    .A3(subtractor_2_out[3]), .A2(subtractor_2_out[2]), .A1(subtractor_2_out[1]), .A0(subtractor_2_out[0]),
    .S3(unitsm_1_s0[3]), .S2(unitsm_1_s0[2]), .S1(unitsm_1_s0[1]), .S0(unitsm_1_s0[0]), .VAI1(unitsm_1_vai1));
  Subtractor #(.width(4)) subtractor_2 (
    .a(register_2_q), .b(4'b0000), .out(subtractor_2_out), .bin(decsm_2_vai1));  // open: bout
  Hex_Digit_Display hex_digit_display_3 (.value(decsm_2_s0));  // open: dp
  decSM decsm_2 (
    .A3(subtractor_3_out[3]), .A2(subtractor_3_out[2]), .A1(subtractor_3_out[1]), .A0(subtractor_3_out[0]),
    .S3(decsm_2_s0[3]), .S2(decsm_2_s0[2]), .S1(decsm_2_s0[1]), .S0(decsm_2_s0[0]), .VAI1(decsm_2_vai1));
  Register #(.width(4)) register_3 (.D(decsm_2_s0), .Q(register_3_q), .clk(and_1_out), .clr(CLEAR));  // open: en
  Subtractor #(.width(4)) subtractor_3 (
    .a(register_3_q), .b(4'b0000), .out(subtractor_3_out), .bin(unitsm_2_vai1));  // open: bout
  Hex_Digit_Display hex_digit_display_4 (.value(unitsm_2_s0));  // open: dp
  unitSM unitsm_2 (
    .A3(adder_1_out[3]), .A2(adder_1_out[2]), .A1(adder_1_out[1]), .A0(adder_1_out[0]), .S3(unitsm_2_s0[3]),
    .S2(unitsm_2_s0[2]), .S1(unitsm_2_s0[1]), .S0(unitsm_2_s0[0]), .VAI1(unitsm_2_vai1));
  Register #(.width(4)) register_4 (.D(unitsm_2_s0), .Q(register_4_q), .clk(and_1_out), .clr(CLEAR));  // open: en
  Adder #(.width(4)) adder_1 (.a(4'b1111), .b(register_4_q), .out(adder_1_out));  // open: cin, cout
endmodule

module unitSM (
  input  A3,
  input  A2,
  input  A1,
  input  A0,
  output S3,
  output S2,
  output S1,
  output S0,
  output VAI1
);

  wire and_1_out, and_2_out, and_3_out, and_4_out, and_5_out, and_6_out, and_7_out, and_8_out, and_9_out,
       and_10_out, and_11_out, not_1_out, not_2_out, not_3_out, not_4_out, not_5_out, not_6_out, not_7_out,
       not_8_out;

  not not_1 (not_1_out, A3);
  not not_2 (not_2_out, A0);
  not not_3 (not_3_out, A3);
  not not_4 (not_4_out, A2);
  not not_5 (not_5_out, A0);
  not not_6 (not_6_out, A3);
  not not_7 (not_7_out, A2);
  not not_8 (not_8_out, A0);
  and and_1 (and_1_out, A3, A1);
  and and_2 (and_2_out, A3, A2);
  and and_3 (and_3_out, not_1_out, A2);
  or or_1 (S2, and_3_out, and_4_out);
  and and_4 (and_4_out, A2, not_2_out);
  and and_5 (and_5_out, not_3_out, A1);
  and and_6 (and_6_out, not_4_out, A1);
  or or_2 (S1, and_5_out, and_6_out, and_7_out);
  and and_7 (and_7_out, A1, not_5_out);
  and and_8 (and_8_out, not_6_out, A0);
  and and_9 (and_9_out, not_7_out, A0);
  and and_10 (and_10_out, A1, A0);
  and and_11 (and_11_out, A3, A2, not_8_out);
  or or_3 (VAI1, and_1_out, and_2_out);
  or or_4 (S0, and_8_out, and_9_out, and_10_out, and_11_out);

  assign S3 = A3;
endmodule

module decSM (
  input  A3,
  input  A2,
  input  A1,
  input  A0,
  output S3,
  output S2,
  output S1,
  output S0,
  output VAI1
);

  wire and_1_out, and_2_out, and_3_out, and_4_out, and_5_out, not_1_out, not_2_out, not_3_out, not_4_out;

  not not_1 (not_1_out, A3);
  not not_2 (not_2_out, A2);
  not not_3 (not_3_out, A0);
  not not_4 (not_4_out, A3);
  and and_1 (and_1_out, not_1_out, A1);
  and and_2 (and_2_out, not_2_out, A1);
  or or_1 (S1, and_1_out, and_2_out, and_3_out);
  and and_3 (and_3_out, A1, not_3_out);
  and and_4 (and_4_out, not_4_out, A0);
  or or_2 (S0, and_4_out, and_5_out);
  and and_5 (and_5_out, A2, A1, A0);

  assign S2 = A2;
  assign S3 = 1'b0;
  assign VAI1 = A3;
endmodule
